# Fritzing sketch bareduinoPCBV3 (saved by Fritzing 0.9.2b)
circuit board: 6.52464cm x 4.39378cm
breadboards: 1

parts:
  RF_plug2 = double row female pin header, 8 pins [form="♀ (female)"]
  locker_detect_plug = female pin header, 2 pins [form="♀ (female)"]
  RFID_plug = female pin header, 3 pins [form="♀ (female)"]
  battery_plug = female pin header, 3 pins [form="♀ (female)"]
  U3 = atmega328 [package=dip]
  C_22nF4 = Ceramic Capacitor [capacitance=22nF package="100 mil [THT, multilayer]"]
  XTAL4 = Crystal [frequency="16 Mhz" package=THT]
  stab_Vreg2 = Electrolytic Capacitor [capacitance=22µF voltage=6.3V package="100 mil [THT, electrolytic]"]
  VREG = MCP1755ST [package=sot223]
  Button_LED_plug2 = double row female pin header, 6 pins [form="♀ (female)"]
  servo_plug = female pin header, 3 pins [form="♀ (female)"]
  C_22nF5 = Ceramic Capacitor [capacitance=22nF package="100 mil [THT, multilayer]"]
  C_22nF6 = Ceramic Capacitor [capacitance=22nF package="100 mil [THT, multilayer]"]
  NPN_RFID2 = NPN-Transistor [package="TO92 [THT]"]
  R6 = Resistor [tolerance=±5% resistance=330 package=THT]
  stab_RF2 = Electrolytic Capacitor [capacitance=22µF voltage=6.3V package="100 mil [THT, electrolytic]"]
  J3 = female pin header, 3 pins [form="♀ (female)"]
  R7 = Resistor [tolerance=±5% resistance=10k package=THT]
  v_mesure = Resistor [tolerance=±5% resistance=22k package=THT]
  pd2 = Resistor [tolerance=±5% resistance=220 package=THT]
  NPN_servo = NPN-Transistor [package="TO92 [THT]"]
  R8 = Resistor [tolerance=±5% resistance=330 package=THT]

nets:
  GND: RF_plug2.pin1, locker_detect_plug.pin2, battery_plug.pin2, U3.GND, C_22nF4.1, stab_Vreg2.-, VREG.GND, Button_LED_plug2.pin1, C_22nF5.0, C_22nF6.0, NPN_RFID2.B, stab_RF2.-, pd2.Pin_1, NPN_servo.B
  N1: RF_plug2.pin2, RFID_plug.pin2, battery_plug.pin1, U3.VCC, U3.AVCC, C_22nF4.0, stab_Vreg2.+, VREG.OUT, Button_LED_plug2.pin4, servo_plug.pin2, stab_RF2.+, R7.Pin_1
  N2: RF_plug2.pin4, U3.D13
  N3: RF_plug2.pin5, U3.D12
  N4: RF_plug2.pin6, U3.D11_(PWM)
  N5: RF_plug2.pin7, U3.D10_(PWM)
  N6: RF_plug2.pin8, U3.D9_(PWM)
  N7: locker_detect_plug.pin1, U3.A2
  N8: RFID_plug.pin1, U3.D8
  N9: RFID_plug.pin3, NPN_RFID2.E
  N10: battery_plug.pin3, VREG.IN, v_mesure.Pin_1
  N11: U3.RESET, J3.pin1, R7.Pin_0
  N12: U3.D0_(RX), J3.pin2
  N13: U3.D1_(TX), J3.pin3
  N14: U3.D3_(PWM), R6.Pin_1
  N15: U3.XLAT1, XTAL4.pin_1, C_22nF6.1
  N16: U3.XLAT2, XTAL4.pin_0, C_22nF5.1
  N17: U3.D5_(PWM), Button_LED_plug2.pin6
  N18: U3.D6_(PWM), servo_plug.pin1
  N19: U3.D7, R8.Pin_1
  N20: U3.A0, Button_LED_plug2.pin2
  N21: U3.A1, Button_LED_plug2.pin3
  N22: U3.A3, v_mesure.Pin_0, pd2.Pin_0
  N23: servo_plug.pin3, NPN_servo.E
  N24: NPN_RFID2.C, R6.Pin_0
  N25: NPN_servo.C, R8.Pin_0

custom parts:
  MCP1755ST: http://be.farnell.com/fr-BE/microchip/mcp1755st-3302e-db/ic-ldo-volt-reg-3-3v-0-3a-sot223/dp/2306609
