# Fritzing sketch bareduino_naked (saved by Fritzing 0.9.2b)
circuit board: 6.50385cm x 3.75cm
breadboards: 1

parts:
  XTAL2 = Crystal [frequency="16 Mhz" package=THT]
  button_plug = female pin header, 3 pins [form="♀ (female)"]
  RF_plug = double row female pin header, 8 pins [form="♀ (female)"]
  VREG1 = MCP1755ST [package=sot223]
  servo_plug = female pin header, 3 pins [form="♀ (female)"]
  LED_plug = female pin header, 3 pins [form="♀ (female)"]
  battery_plug = female pin header, 2 pins [form="♀ (female)"]
  C_22nF = Ceramic Capacitor [capacitance=22nF package="100 mil [THT, multilayer]"]
  stab_RF = Electrolytic Capacitor [capacitance=22µF voltage=6.3V package="100 mil [THT, electrolytic]"]
  C_22nF_2 = Ceramic Capacitor [capacitance=22nF package="100 mil [THT, multilayer]"]
  C_22nF_3 = Ceramic Capacitor [capacitance=22nF package="100 mil [THT, multilayer]"]
  NPN_servo = NPN-Transistor [package="TO92 [THT]"]  # not connected
  NPN_RFID = NPN-Transistor [package="TO92 [THT]"]
  R2 = Resistor [tolerance=±5% resistance=330 package=THT]
  stab_Vreg = Electrolytic Capacitor [capacitance=22µF voltage=6.3V package="100 mil [THT, electrolytic]"]
  U1 = atmega328 [package=dip]
  R3 = Resistor [tolerance=±5% resistance=10k package=THT]
  J1 = female pin header, 3 pins [form="♀ (female)"]
  RFID_plug = female pin header, 3 pins [form="♀ (female)"]
  locker_detector_plug = female pin header, 2 pins [form="♀ (female)"]

nets:
  N1: XTAL2.pin_0, C_22nF_2.0, U1.XLAT2
  N2: XTAL2.pin_1, C_22nF_3.1, U1.XLAT1
  N3: button_plug.pin1, U1.A1
  N4: button_plug.pin2, U1.A0
  GND: button_plug.pin3, RF_plug.pin8, VREG1.GND, LED_plug.pin2, battery_plug.pin2, C_22nF.1, stab_RF.-, C_22nF_3.0, NPN_RFID.B, stab_Vreg.-, U1.GND, locker_detector_plug.pin1
  N5: RF_plug.pin1, VREG1.OUT, servo_plug.pin2, LED_plug.pin3, C_22nF.0, stab_RF.+, stab_Vreg.+, U1.VCC, U1.AVCC, R3.Pin_0, RFID_plug.pin2
  N6: RF_plug.pin3, U1.D13
  N7: RF_plug.pin4, U1.D12
  N8: RF_plug.pin5, U1.D11_(PWM)
  N9: RF_plug.pin6, U1.D10_(PWM)
  N10: RF_plug.pin7, U1.D9_(PWM)
  N11: VREG1.IN, battery_plug.pin1
  N12: servo_plug.pin1, NPN_RFID.E, RFID_plug.pin3
  N13: servo_plug.pin3, U1.D5_(PWM)
  N14: LED_plug.pin1, U1.D6_(PWM)
  N15: NPN_RFID.C, R2.Pin_0
  N16: R2.Pin_1, U1.D4
  N17: U1.RESET, R3.Pin_1, J1.pin1
  N18: U1.D0_(RX), J1.pin2
  N19: U1.D1_(TX), J1.pin3
  N20: U1.D8, RFID_plug.pin1
  N21: U1.A2, locker_detector_plug.pin2

custom parts:
  MCP1755ST: http://be.farnell.com/fr-BE/microchip/mcp1755st-3302e-db/ic-ldo-volt-reg-3-3v-0-3a-sot223/dp/2306609
