# Fritzing sketch bike_PCB (saved by Fritzing 0.9.2b)
breadboards: 1

parts:
  U1 = atmega328 [package=dip]
  V_REG = Voltage Regulator LDO [package=sot23-5]
  Battery = LIPO-1000mAh [package=lipo-1000]
  Cap22nF = Ceramic Capacitor [capacitance="100 nF" voltage=6.3V package="0805 [SMD, multilayer]"]

nets:
  N1: U1.VCC, U1.AVCC, V_REG.OUT, Cap22nF.0
  GND: U1.GND, V_REG.GND, Battery.-, Cap22nF.1
  N2: V_REG.IN, V_REG.EN, Battery.+
